# Fritzing sketch OSL12306_16_plus (saved by Fritzing 1.0.2b)
breadboards: 1

parts:
  LED1 = LED - 5mm [color="Red (633nm)" current=0.030A package="5 mm [THT]"]
  LED2 = LED - 5mm [color="Red (633nm)" current=0.030A package="5 mm [THT]"]
  LED3 = LED - 5mm [color="Red (633nm)" current=0.030A package="5 mm [THT]"]
  LED4 = LED - 5mm [color="Red (633nm)" current=0.030A package="5 mm [THT]"]
  LED5 = LED - 5mm [color="Red (633nm)" current=0.030A package="5 mm [THT]"]
  Arduino_Mega = Arduino Mega 2560 (Rev3)
  LED6 = LED - 5mm [color="Red (633nm)" current=0.030A package="5 mm [THT]"]
  LED7 = LED - 5mm [color="Red (633nm)" current=0.030A package="5 mm [THT]"]
  LED8 = LED - 5mm [color="Red (633nm)" current=0.030A package="5 mm [THT]"]
  LED9 = LED - 5mm [color="Red (633nm)" current=0.030A package="5 mm [THT]"]
  LED10 = LED - 5mm [color="Red (633nm)" current=0.030A package="5 mm [THT]"]
  LED11 = LED - 5mm [color="Red (633nm)" current=0.030A package="5 mm [THT]"]
  LED12 = LED - 5mm [color="Red (633nm)" current=0.030A package="5 mm [THT]"]
  LED13 = LED - 5mm [color="Red (633nm)" current=0.030A package="5 mm [THT]"]
  LED14 = LED - 5mm [color="Red (633nm)" current=0.030A package="5 mm [THT]"]
  LED15 = LED - 5mm [color="Red (633nm)" current=0.030A package="5 mm [THT]"]
  LED16 = LED - 5mm [color="Red (633nm)" current=0.030A package="5 mm [THT]"]
  R1 = Resistor [tolerance=±5% power=0.25W resistance=15 package=THT]
  R2 = Resistor [tolerance=±5% power=0.25W resistance=15 package=THT]
  R3 = Resistor [tolerance=±5% power=0.25W resistance=15 package=THT]
  R4 = Resistor [tolerance=±5% power=0.25W resistance=15 package=THT]
  R5 = Resistor [tolerance=±5% power=0.25W resistance=15 package=THT]
  R6 = Resistor [tolerance=±5% power=0.25W resistance=15 package=THT]
  R7 = Resistor [tolerance=±5% power=0.25W resistance=15 package=THT]
  R8 = Resistor [tolerance=±5% power=0.25W resistance=15 package=THT]
  R9 = Resistor [tolerance=±5% power=0.25W resistance=15 package=THT]
  R10 = Resistor [tolerance=±5% power=0.25W resistance=15 package=THT]
  R11 = Resistor [tolerance=±5% power=0.25W resistance=15 package=THT]
  R12 = Resistor [tolerance=±5% power=0.25W resistance=15 package=THT]
  R13 = Resistor [tolerance=±5% power=0.25W resistance=15 package=THT]
  R14 = Resistor [tolerance=±5% power=0.25W resistance=15 package=THT]
  R15 = Resistor [tolerance=±5% power=0.25W resistance=15 package=THT]
  R16 = Resistor [tolerance=±5% power=0.25W resistance=15 package=THT]
  LED17 = LED - 5mm [color="Green (555nm)" current=0.030A package="5 mm [THT]"]
  Q1 = NPN-Transistor [package="TO92 [THT]"]

nets:
  D23: LED1.cathode, Arduino_Mega.D23, R1.Pin_0
  N1: LED1.anode, LED2.anode, LED3.anode, LED4.anode, LED5.anode, LED6.anode, LED7.anode, LED8.anode, LED9.anode, LED10.anode, LED11.anode, LED12.anode, LED13.anode, LED14.anode, LED15.anode, LED16.anode, LED17.cathode, Q1.E
  D22: LED2.cathode, Arduino_Mega.D22, R2.Pin_0
  D24: LED3.cathode, Arduino_Mega.D24, R3.Pin_0
  D25: LED4.cathode, Arduino_Mega.D25, R4.Pin_0
  D27: LED5.cathode, Arduino_Mega.D27, R5.Pin_0
  GND: Arduino_Mega.GND, R1.Pin_1, R2.Pin_1, R3.Pin_1, R4.Pin_1, R5.Pin_1, R6.Pin_1, R7.Pin_1, R8.Pin_1, R9.Pin_1, R10.Pin_1, R11.Pin_1, R12.Pin_1, R13.Pin_1, R14.Pin_1, R15.Pin_1, R16.Pin_1
  5V: Arduino_Mega.5V, Q1.C
  D26: Arduino_Mega.D26, LED6.cathode, R6.Pin_0
  D28: Arduino_Mega.D28, LED8.cathode, R8.Pin_0
  D29: Arduino_Mega.D29, LED7.cathode, R7.Pin_0
  D30: Arduino_Mega.D30, LED10.cathode, R10.Pin_0
  D31: Arduino_Mega.D31, LED9.cathode, R9.Pin_0
  D32: Arduino_Mega.D32, LED12.cathode, R12.Pin_0
  D33: Arduino_Mega.D33, LED11.cathode, R11.Pin_0
  D34: Arduino_Mega.D34, LED14.cathode, R14.Pin_0
  D35: Arduino_Mega.D35, LED13.cathode, R13.Pin_0
  D36: Arduino_Mega.D36, LED16.cathode, R16.Pin_0
  D37: Arduino_Mega.D37, LED15.cathode, R15.Pin_0
  DP: Arduino_Mega.D38, LED17.anode
  SW: Arduino_Mega.D40, Q1.B
