# Fritzing sketch OSL20541-IR (saved by Fritzing 1.0.2b)
breadboards: 2

parts:
  LED1 = LED - 5mm [color="Red (633nm)" current=0.030A package="5 mm [THT]"]
  LED2 = LED - 5mm [color="Red (633nm)" current=0.030A package="5 mm [THT]"]
  LED3 = LED - 5mm [color="Red (633nm)" current=0.030A package="5 mm [THT]"]
  LED4 = LED - 5mm [color="Red (633nm)" current=0.030A package="5 mm [THT]"]
  LED5 = LED - 5mm [color="Red (633nm)" current=0.030A package="5 mm [THT]"]
  Arduino_Mega = Arduino Mega 2560 (Rev3)
  LED6 = LED - 5mm [color="Red (633nm)" current=0.030A package="5 mm [THT]"]
  LED7 = LED - 5mm [color="Red (633nm)" current=0.030A package="5 mm [THT]"]
  LED8 = LED - 5mm [color="Red (633nm)" current=0.030A package="5 mm [THT]"]
  LED9 = LED - 5mm [color="Red (633nm)" current=0.030A package="5 mm [THT]"]
  LED10 = LED - 5mm [color="Red (633nm)" current=0.030A package="5 mm [THT]"]
  LED11 = LED - 5mm [color="Red (633nm)" current=0.030A package="5 mm [THT]"]
  LED12 = LED - 5mm [color="Red (633nm)" current=0.030A package="5 mm [THT]"]
  LED13 = LED - 5mm [color="Red (633nm)" current=0.030A package="5 mm [THT]"]
  LED14 = LED - 5mm [color="Red (633nm)" current=0.030A package="5 mm [THT]"]
  R1 = Resistor [tolerance=±5% power=0.25W resistance=150 package=THT]
  R2 = Resistor [tolerance=±5% power=0.25W resistance=150 package=THT]
  R3 = Resistor [tolerance=±5% power=0.25W resistance=150 package=THT]
  R4 = Resistor [tolerance=±5% power=0.25W resistance=150 package=THT]
  R5 = Resistor [tolerance=±5% power=0.25W resistance=150 package=THT]
  R6 = Resistor [tolerance=±5% power=0.25W resistance=150 package=THT]
  R7 = Resistor [tolerance=±5% power=0.25W resistance=150 package=THT]
  R8 = Resistor [tolerance=±5% power=0.25W resistance=150 package=THT]
  R9 = Resistor [tolerance=±5% power=0.25W resistance=150 package=THT]
  R10 = Resistor [tolerance=±5% power=0.25W resistance=150 package=THT]
  R11 = Resistor [tolerance=±5% power=0.25W resistance=150 package=THT]
  R12 = Resistor [tolerance=±5% power=0.25W resistance=150 package=THT]
  R13 = Resistor [tolerance=±5% power=0.25W resistance=150 package=THT]
  R14 = Resistor [tolerance=±5% power=0.25W resistance=150 package=THT]
  LED17 = LED - 5mm [color="Green (555nm)" current=0.030A package="5 mm [THT]"]
  R15 = Resistor [tolerance=±5% power=0.25W resistance=150 package=THT]
  LED18 = LED - 5mm [color="Red (633nm)" current=0.030A package="5 mm [THT]"]
  LED19 = LED - 5mm [color="Red (633nm)" current=0.030A package="5 mm [THT]"]
  LED20 = LED - 5mm [color="Red (633nm)" current=0.030A package="5 mm [THT]"]
  LED21 = LED - 5mm [color="Red (633nm)" current=0.030A package="5 mm [THT]"]
  LED22 = LED - 5mm [color="Red (633nm)" current=0.030A package="5 mm [THT]"]
  LED23 = LED - 5mm [color="Red (633nm)" current=0.030A package="5 mm [THT]"]
  LED24 = LED - 5mm [color="Red (633nm)" current=0.030A package="5 mm [THT]"]
  LED25 = LED - 5mm [color="Red (633nm)" current=0.030A package="5 mm [THT]"]
  LED26 = LED - 5mm [color="Red (633nm)" current=0.030A package="5 mm [THT]"]
  LED27 = LED - 5mm [color="Red (633nm)" current=0.030A package="5 mm [THT]"]
  LED28 = LED - 5mm [color="Red (633nm)" current=0.030A package="5 mm [THT]"]
  LED29 = LED - 5mm [color="Red (633nm)" current=0.030A package="5 mm [THT]"]
  LED30 = LED - 5mm [color="Red (633nm)" current=0.030A package="5 mm [THT]"]
  LED31 = LED - 5mm [color="Red (633nm)" current=0.030A package="5 mm [THT]"]
  LED32 = LED - 5mm [color="Green (555nm)" current=0.030A package="5 mm [THT]"]

nets:
  D23: LED1.cathode, Arduino_Mega.D23, R1.Pin_0, LED18.cathode
  D36: LED1.anode, LED2.anode, LED3.anode, LED4.anode, LED5.anode, Arduino_Mega.D36, LED6.anode, LED7.anode, LED8.anode, LED9.anode, LED10.anode, LED11.anode, LED12.anode, LED13.anode, LED14.anode, LED17.anode
  D22: LED2.cathode, Arduino_Mega.D22, R2.Pin_0, LED19.cathode
  D24: LED3.cathode, Arduino_Mega.D24, R3.Pin_0, LED20.cathode
  D25: LED4.cathode, Arduino_Mega.D25, R4.Pin_0, LED21.cathode
  D27: LED5.cathode, Arduino_Mega.D27, R5.Pin_0, LED31.cathode
  GND: Arduino_Mega.GND, R1.Pin_1, R2.Pin_1, R3.Pin_1, R4.Pin_1, R5.Pin_1, R6.Pin_1, R7.Pin_1, R8.Pin_1, R9.Pin_1, R10.Pin_1, R11.Pin_1, R12.Pin_1, R13.Pin_1, R14.Pin_1, R15.Pin_1
  D26: Arduino_Mega.D26, LED6.cathode, R6.Pin_0, LED30.cathode
  D28: Arduino_Mega.D28, LED8.cathode, R8.Pin_0, LED28.cathode
  D29: Arduino_Mega.D29, LED7.cathode, R7.Pin_0, LED29.cathode
  D30: Arduino_Mega.D30, LED10.cathode, R10.Pin_0, LED26.cathode
  D31: Arduino_Mega.D31, LED9.cathode, R9.Pin_0, LED27.cathode
  D32: Arduino_Mega.D32, LED12.cathode, R12.Pin_0, LED24.cathode
  D33: Arduino_Mega.D33, LED11.cathode, R11.Pin_0, LED25.cathode
  D34: Arduino_Mega.D34, LED14.cathode, R14.Pin_0, LED22.cathode
  D35: Arduino_Mega.D35, LED13.cathode, R13.Pin_0, LED23.cathode
  DP: Arduino_Mega.D38, LED17.cathode, R15.Pin_0, LED32.cathode
  D40: Arduino_Mega.D40, LED18.anode, LED19.anode, LED20.anode, LED21.anode, LED22.anode, LED23.anode, LED24.anode, LED25.anode, LED26.anode, LED27.anode, LED28.anode, LED29.anode, LED30.anode, LED31.anode, LED32.anode
