# Fritzing sketch OSL30561-IRA (saved by Fritzing 1.0.2b)
breadboards: 3

parts:
  R1 = Resistor [tolerance=±5% power=0.25W resistance=150 package=THT]
  R2 = Resistor [tolerance=±5% power=0.25W resistance=150 package=THT]
  R3 = Resistor [tolerance=±5% power=0.25W resistance=150 package=THT]
  R4 = Resistor [tolerance=±5% power=0.25W resistance=150 package=THT]
  R5 = Resistor [tolerance=±5% power=0.25W resistance=150 package=THT]
  R6 = Resistor [tolerance=±5% power=0.25W resistance=150 package=THT]
  R7 = Resistor [tolerance=±5% power=0.25W resistance=150 package=THT]
  R8 = Resistor [tolerance=±5% power=0.25W resistance=150 package=THT]
  LED1 = LED - 5mm [color="Red (633nm)" current=0.030A package="5 mm [THT]"]
  LED2 = LED - 5mm [color="Red (633nm)" current=0.030A package="5 mm [THT]"]
  LED3 = LED - 5mm [color="Red (633nm)" current=0.030A package="5 mm [THT]"]
  LED4 = LED - 5mm [color="Red (633nm)" current=0.030A package="5 mm [THT]"]
  LED5 = LED - 5mm [color="Red (633nm)" current=0.030A package="5 mm [THT]"]
  LED6 = LED - 5mm [color="Red (633nm)" current=0.030A package="5 mm [THT]"]
  LED7 = LED - 5mm [color="Red (633nm)" current=0.030A package="5 mm [THT]"]
  LED8 = LED - 5mm [color="Green (555nm)" current=0.030A package="5 mm [THT]"]
  LED9 = LED - 5mm [color="Red (633nm)" current=0.030A package="5 mm [THT]"]
  LED10 = LED - 5mm [color="Red (633nm)" current=0.030A package="5 mm [THT]"]
  LED11 = LED - 5mm [color="Red (633nm)" current=0.030A package="5 mm [THT]"]
  LED12 = LED - 5mm [color="Red (633nm)" current=0.030A package="5 mm [THT]"]
  LED13 = LED - 5mm [color="Red (633nm)" current=0.030A package="5 mm [THT]"]
  LED14 = LED - 5mm [color="Red (633nm)" current=0.030A package="5 mm [THT]"]
  LED15 = LED - 5mm [color="Red (633nm)" current=0.030A package="5 mm [THT]"]
  LED16 = LED - 5mm [color="Green (555nm)" current=0.030A package="5 mm [THT]"]
  LED17 = LED - 5mm [color="Red (633nm)" current=0.030A package="5 mm [THT]"]
  LED18 = LED - 5mm [color="Red (633nm)" current=0.030A package="5 mm [THT]"]
  LED19 = LED - 5mm [color="Red (633nm)" current=0.030A package="5 mm [THT]"]
  LED20 = LED - 5mm [color="Red (633nm)" current=0.030A package="5 mm [THT]"]
  LED21 = LED - 5mm [color="Red (633nm)" current=0.030A package="5 mm [THT]"]
  LED22 = LED - 5mm [color="Red (633nm)" current=0.030A package="5 mm [THT]"]
  LED23 = LED - 5mm [color="Red (633nm)" current=0.030A package="5 mm [THT]"]
  LED24 = LED - 5mm [color="Green (555nm)" current=0.030A package="5 mm [THT]"]
  パーツ1 = Arduino Mega 2560 (Rev3)

nets:
  LED1: R1.Pin_0, LED1.cathode, LED9.cathode, LED17.cathode, パーツ1.D41
  N1: R1.Pin_1, R2.Pin_1, R3.Pin_1, R4.Pin_1, R5.Pin_1, R6.Pin_1, R7.Pin_1, R8.Pin_1, パーツ1.GND
  LED2: R2.Pin_0, LED2.cathode, LED10.cathode, LED18.cathode, パーツ1.D39
  N2: R3.Pin_0, LED3.cathode, LED11.cathode, LED19.cathode, パーツ1.D37
  N3: R4.Pin_0, LED4.cathode, LED12.cathode, LED20.cathode, パーツ1.D35
  N4: R5.Pin_0, LED5.cathode, LED13.cathode, LED21.cathode
  N5: R6.Pin_0, LED6.cathode, LED14.cathode, LED22.cathode, パーツ1.D33
  N6: R7.Pin_0, LED7.cathode, LED15.cathode, LED23.cathode, パーツ1.D31
  N7: R8.Pin_0, LED8.cathode, LED16.cathode, LED24.cathode, パーツ1.D29
  Digit1: LED1.anode, LED2.anode, LED3.anode, LED4.anode, LED5.anode, LED6.anode, LED7.anode, LED8.anode, パーツ1.D27
  Digit2: LED9.anode, LED10.anode, LED11.anode, LED12.anode, LED13.anode, LED14.anode, LED15.anode, LED16.anode, パーツ1.D25
  Digit3: LED17.anode, LED18.anode, LED19.anode, LED20.anode, LED21.anode, LED22.anode, LED23.anode, LED24.anode, パーツ1.D23
